# Fritzing sketch D-8_servo_s-1 (saved by Fritzing 0.9.2b)

parts:
  パーツ1 = Arduino Uno (Rev3)
  J1 = Basic Servo
  U1 = LCD-16X2 [package=lcd-16x2_noholes]  # not connected

nets:
  N1: パーツ1.D6_PWM, J1.vcc
  N2: パーツ1.5V, J1.pulse
  GND: パーツ1.GND, J1.gnd
